# Fritzing sketch Schematic (saved by Fritzing 0.9.3b)
breadboards: 1

parts:
  Part1 = Arduino Uno (Rev3) - ICSP
  LCD1 = LCD screen
  U1 = TMP36 [package=to-92]
  Q1 = NPN-Transistor [package="TO92 [THT]"]
  R1 = Resistor [tolerance=±5% resistance=220 package="1206 [SMD]"]
  U2 = POT [package=pot_alpha_rv16af-20]
  M1 = DC Motor
  D1 = Diode [package=diode-1n4148]
  VCC1 = Battery block 9V

nets:
  N1: Part1.A0, U1.VOUT
  N2: Part1.ICSP_MISO, Part1.D12/MISO, LCD1.RS
  5V: Part1.5V, LCD1.VDD, LCD1.LED+, U1.VCC, U2.A, M1.pin_1, D1.C, VCC1.+
  N3: Part1.ICSP_MOSI, Part1.D11_PWM/MOSI, LCD1.E
  GND: Part1.GND, LCD1.VSS, LCD1.R/W, U1.GND, Q1.E, VCC1.-
  N4: Part1.D10_PWM/SS, R1.Pin_1
  N5: Part1.D2, LCD1.DB7
  N6: Part1.D3_PWM, LCD1.DB6
  N7: Part1.D4, LCD1.DB5
  N8: Part1.D5_PWM, LCD1.DB4
  N9: LCD1.V0, U2.S
  N10: LCD1.LED-, U2.E
  N11: Q1.B, R1.Pin_0
  N12: Q1.C, M1.pin_2, D1.A
