# Fritzing sketch cs207schematic (saved by Fritzing 0.9.3b)
breadboards: 1

parts:
  Q1 = NPN-Transistor [package="TO92 [THT]"]
  Part1 = Arduino Uno (Rev3) - ICSP
  R1 = Resistor [tolerance=±5% resistance=220 package="0805 [SMD]"]
  LCD1 = LCD screen
  T1 = TMP36 Temperature Sensor [package="TO92 [THT]"]
  M1 = DC Motor
  D1 = Diode [package=diode-1n4148]
  VCC1 = Battery block 9V
  U1 = POT [package=pot_alpha_rv16af-20]

nets:
  N1: Q1.E, M1.pin_2, D1.A
  N2: Q1.B, R1.Pin_0
  GND: Q1.C, Part1.GND, LCD1.LED+, T1.GND, VCC1.-, U1.S
  N3: Part1.A0, T1.Vout
  N4: Part1.ICSP_MOSI, Part1.D11_PWM/MOSI, LCD1.E
  5V: Part1.5V, LCD1.VDD, LCD1.LED-, T1.+Vs, M1.pin_1, D1.C, VCC1.+, U1.A
  N5: Part1.D10_PWM/SS, R1.Pin_1
  N6: Part1.D12/MISO, LCD1.RS
  N7: Part1.D2, LCD1.DB7
  N8: Part1.D3_PWM, LCD1.DB6
  N9: Part1.D4, LCD1.DB5
  N10: Part1.D5_PWM, LCD1.DB4
  N11: LCD1.V0, U1.E
